# Fritzing sketch CareE (saved by Fritzing 1.0.1rc)
breadboards: 1

parts:
  Componente1 = Arduino Uno (Rev3)
  A1 = Raspberry Pi 5
  Componente2 = SRF05 Ultrasonic Rangefinder
  Componente3 = SRF05 Ultrasonic Rangefinder
  Componente4 = SRF05 Ultrasonic Rangefinder
  J1 = XT60 Connector [package=THT]
  PWM1 = PCA9685 16x12-bit PWM Breakout
  J2 = Basic Servo
  J3 = Basic Servo
  J4 = Basic Servo
  J5 = Basic Servo
  J6 = Basic Servo
  J7 = Basic Servo
  J8 = Basic Servo
  J9 = Basic Servo
  J10 = Basic Servo
  U1 = LM2596 step down module
  U2 = LM2596 step down module
  DC_Mot_Enc1 = DC Motor with two-phase hall-encoder [part_number=VT-E-G25A-06-177E]
  DC_Mot_Enc2 = DC Motor with two-phase hall-encoder [part_number=VT-E-G25A-06-177E]
  A2 = drv-1012
  A3 = drv-1012

nets:
  N1: Componente1.A0, DC_Mot_Enc1.pin3
  N2: Componente1.A1, DC_Mot_Enc1.pin4
  N3: Componente1.A2, DC_Mot_Enc2.pin3
  N4: Componente1.A3, DC_Mot_Enc2.pin4
  N5: Componente1.A4/SDA, A3.Pin_3
  N6: Componente1.A5/SCL, A3.Pin_7
  N7: Componente1.D8, A2.Pin_8
  N8: Componente1.D9_PWM, A2.Pin_4
  N9: Componente1.D10_PWM/SS, A2.Pin_7
  N10: Componente1.D11_PWM/MOSI, A3.Pin_8
  N11: Componente1.D12/MISO, A3.Pin_4
  N12: Componente1.D13/SCK, A2.Pin_3
  N13: Componente1.D0/RX, A1.GPIO14
  N14: Componente1.D1/TX, A1.GPIO15
  N15: Componente1.D2, Componente3.Trig
  N16: Componente1.D3_PWM, Componente3.Echo
  N17: Componente1.D4, Componente2.Trig
  N18: Componente1.D5_PWM, Componente2.Echo
  N19: Componente1.D6_PWM, Componente4.Trig
  N20: Componente1.D7, Componente4.Echo
  VCC: Componente1.5V, A1.5V, A1.Fan-5V, Componente2.VCC, Componente3.VCC, Componente4.VCC, PWM1.no_name_yet#505, U1.OUT+, DC_Mot_Enc1.pin2, DC_Mot_Enc2.pin2, A2.Pin_5, A3.Pin_5
  GND: Componente1.GND, A1.GND, Componente2.GND, Componente3.GND, Componente4.GND, J1.GND, PWM1.no_name_yet#501, PWM1.no_name_yet#1000, PWM1.no_name_yet#1001, PWM1.no_name_yet#1002, PWM1.no_name_yet#1003, PWM1.no_name_yet#1004, PWM1.no_name_yet#1005, PWM1.no_name_yet#1007, PWM1.no_name_yet#1008, U1.IN-, U1.OUT-, U2.IN-, U2.OUT-, DC_Mot_Enc1.pin5, DC_Mot_Enc2.pin5, A2.Pin_1, A2.Pin_9, A3.Pin_1, A3.Pin_9
  N21: A1.GPIO2, PWM1.no_name_yet#504
  N22: A1.GPIO3, PWM1.no_name_yet#503
  N23: J1.VCC, U1.IN+, U2.IN+, A2.Pin_10, A3.Pin_10
  N24: PWM1.no_name_yet#0, J2.pulse
  N25: PWM1.no_name_yet#1, J3.pulse
  N26: PWM1.no_name_yet#2, J4.pulse
  N27: PWM1.no_name_yet#3, J5.pulse
  N28: PWM1.no_name_yet#4, J6.pulse
  N29: PWM1.no_name_yet#5, J7.pulse
  N30: PWM1.no_name_yet#6, J8.pulse
  N31: PWM1.no_name_yet#7, J9.pulse
  N32: PWM1.no_name_yet#8, J10.pulse
  N33: PWM1.no_name_yet#100, PWM1.no_name_yet#101, PWM1.no_name_yet#102, PWM1.no_name_yet#103, PWM1.no_name_yet#104, PWM1.no_name_yet#105, PWM1.no_name_yet#106, PWM1.no_name_yet#107, PWM1.no_name_yet#108, PWM1.no_name_yet#506, U2.OUT+
  N34: DC_Mot_Enc1.pin1, A2.Pin_12
  N35: DC_Mot_Enc1.pin6, A2.Pin_11
  N36: DC_Mot_Enc2.pin1, A3.Pin_12
  N37: DC_Mot_Enc2.pin6, A3.Pin_11

custom parts:
  Raspberry Pi 5: The RPi5, a faster version of the awesome Raspberry Pi4B ARM Board with 40 pin gpio.
  XT60 Connector: Yellow XT60 connector for high current loads up to 40A
  LM2596 step down module: LM2596 DC-DC step down power supply module 3 A.
  drv-1012: .The BTS7960 is a fully integrated high current H bridge module for motor drive applications.
