# Fritzing sketch motors_drivers (saved by Fritzing 1.0.1rc)
breadboards: 1

parts:
  Componente1 = Arduino Uno (Rev3)
  M1 = BTS7960
  M2 = BTS7960
  DC_Mot_Enc1 = DC Motor with two-phase hall-encoder [part_number=VT-E-G25A-06-177E]
  DC_Mot_Enc2 = DC Motor with two-phase hall-encoder [part_number=VT-E-G25A-06-177E]

nets:
  N1: Componente1.D9_PWM, M1.pin1
  N2: Componente1.D10_PWM/SS, M1.pin2
  N3: Componente1.D12/MISO, DC_Mot_Enc1.pin5
  N4: Componente1.D13/SCK, DC_Mot_Enc2.pin5
  N5: Componente1.D2, DC_Mot_Enc1.pin4
  N6: Componente1.D3_PWM, DC_Mot_Enc2.pin4
  N7: Componente1.D5_PWM, M2.pin1
  N8: Componente1.D6_PWM, M2.pin2
  N9: Componente1.5V, M1.pin3, M1.pin4, M1.pin7, M2.pin3, M2.pin4, M2.pin7, DC_Mot_Enc1.pin3, DC_Mot_Enc2.pin3
  N10: Componente1.GND, M1.pin8, M2.pin8, DC_Mot_Enc1.pin6, DC_Mot_Enc2.pin6
  N11: M1.pin9, DC_Mot_Enc2.pin2
  N12: M1.pin10, DC_Mot_Enc2.pin1
  N13: M2.pin9, DC_Mot_Enc1.pin2
  N14: M2.pin10, DC_Mot_Enc1.pin1

custom parts:
  BTS7960: BTS7960 43A Peak Power H-Bridge PWM Motor Driver
