# Fritzing sketch servos (saved by Fritzing 1.0.1rc)
breadboards: 1

parts:
  Componente1 = Adafruit PCA9685 PWM/Servo Breakout [part_number=815]
  Componente2 = Arduino Uno (Rev3)
  VCC1 = Battery block 9V
  J1 = Basic Servo

nets:
  N1: Componente1.PWRIN, VCC1.+
  GND: Componente1.GND, Componente1.OE, Componente2.GND, VCC1.-, J1.gnd
  VCC: Componente1.VCC, Componente2.5V
  N2: Componente1.SDA, Componente2.A4/SDA
  N3: Componente1.SCL, Componente2.A5/SCL
  N4: Componente1.PWM15, J1.pulse
  N5: Componente1.5.0V, J1.vcc

custom parts:
  Adafruit PCA9685 PWM/Servo Breakout: Using only two pins, control 16 free-running PWM outputs! I2C-controlled PWM driver with a built in clock. Unlike the TLC5940 family, you do not need to continuously send it signal tying up your microcontroller, its completely free running! 5V compliant, which means you can control it from a 3.3V microcontroller and still safely drive up to 6V outputs (this is good for when you want to control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
