# Fritzing sketch ultraso (saved by Fritzing 1.0.1rc)
breadboards: 1

parts:
  Componente2 = Arduino Uno (Rev3)
  Mod1 = HC-SR04 Ultrasonic Distance Sensor
  Mod2 = HC-SR04 Ultrasonic Distance Sensor
  Mod3 = HC-SR04 Ultrasonic Distance Sensor

nets:
  N1: Componente2.A0, Mod1.TRIG
  N2: Componente2.A1, Mod1.ECHO
  N3: Componente2.A2, Mod2.TRIG
  N4: Componente2.A3, Mod2.ECHO
  N5: Componente2.D8, Mod3.TRIG
  GND: Componente2.GND, Mod1.GND, Mod2.GND, Mod3.GND
  N6: Componente2.D7, Mod3.ECHO
  VCC: Componente2.5V, Mod1.VCC, Mod2.VCC, Mod3.VCC

custom parts:
  HC-SR04 Ultrasonic Distance Sensor: The HC-SR04 is an ultrasonic distance sensor. It is capable of providing measurement for ranges of 2cm to 400cm. The module operates at 5V.
